// Logisim project proj.circ as structural Verilog: 2 circuits, main circuit main
module main (
);

  wire and_1_out, clk, debugger_1_p1, mem, not_1_out, r_w, ram_sel, read, word;
  wire [6:0] keyboard_1_data;
  wire [15:0] addr, data, debugger_1_p4, debugger_1_p5, fp, pc, ps, r0, r1, r2, r3, r4, r5, r6, sp;

  // Probe on r0
  // Probe on fp
  Clock clock_1 (.out(clk));
  // Probe on r2
  // Probe on r1
  // Probe on sp
  // Probe on pc
  // CdM_16 cdm_16_1: pin names not known; wires that end beside it: r0, r1, r2, r3, r4, r5, r6, fp, pc, sp, ps, mem, r_w, word, addr
  // Debugger debugger_1: pin names not known; wires that end beside it: debugger_1_p1, 1'b0, clk, debugger_1_p4, debugger_1_p5
  // Probe on r4
  // Probe on r3
  // Probe on ps
  Keyboard keyboard_1 (.clk(clk), .data(keyboard_1_data));  // open: re, clr, avail
  // Probe on r5
  // Probe on r6
  assign data = not_1_out ? debugger_1_p4 : 16'bz;  // Controlled_Buffer controlled_buffer_1
  not not_1 (not_1_out, r_w);
  assign debugger_1_p5 = r_w ? data : 16'bz;  // Controlled_Buffer controlled_buffer_2
  TTY tty_1 (.data(keyboard_1_data), .clk(clk));  // open: we, clr
  \interconnect  interconnect_1 (.addr(addr), .ram(ram_sel));  // open: kb, ter, tim
  and and_1 (and_1_out, mem, ram_sel);
  // RAM ram_1: pin names not known; wires that end beside it: debugger_1_p1, addr, word, and_1_out, clk, read, data

  // Notes on the sheet:
  //   Процессор
  //   Терминал
  //   Устройства
  //   Память
endmodule

module \interconnect  (
  input  [15:0] addr,
  output ram,
  output kb,
  output ter,
  output tim
);

  wire comparator_1_gt, comparator_2_eq, comparator_3_eq, comparator_4_gt, comparator_5_gt, comparator_6_eq,
       not_2_out, not_3_out;

  Comparator #(.width(4), .mode("unsigned")) comparator_1 (
    .a(addr[15:12]), .b(4'b1110), .gt(comparator_1_gt));  // open: eq, lt
  Comparator #(.width(4), .mode("unsigned")) comparator_2 (
    .a(addr[11:8]), .b(4'b0000), .eq(comparator_2_eq));  // open: gt, lt
  Comparator #(.width(4), .mode("unsigned")) comparator_3 (
    .a(addr[7:4]), .b(4'b0000), .eq(comparator_3_eq));  // open: gt, lt
  Comparator #(.width(4), .mode("unsigned")) comparator_4 (
    .a(addr[3:0]), .b(4'b0111), .gt(comparator_4_gt));  // open: eq, lt
  Comparator #(.width(4), .mode("unsigned")) comparator_5 (
    .a(addr[3:0]), .b(4'b1111), .gt(comparator_5_gt));  // open: eq, lt
  Comparator #(.width(4), .mode("unsigned")) comparator_6 (
    .a(addr[7:4]), .b(4'b0001), .eq(comparator_6_eq));  // open: gt, lt
  not not_1 (ram, comparator_1_gt);
  not not_2 (not_2_out, comparator_4_gt);
  not not_3 (not_3_out, comparator_5_gt);
  and and_1 (kb, comparator_1_gt, comparator_2_eq, comparator_3_eq, not_2_out);
  and and_2 (ter, comparator_1_gt, not_3_out, comparator_2_eq, comparator_4_gt, comparator_3_eq);
  and and_3 (tim, comparator_1_gt, comparator_6_eq, comparator_4_gt, comparator_2_eq);

  // Notes on the sheet:
  //   0xF000-0xF007
  //   0xF008-0xF00F
endmodule
